// Logisim project ABB_Insertion.circ as structural Verilog
module BOARD_BIG_ASM (
  output out_1
);

  wire button_1_out, CLK, CLR, d_ff_1_q, not_1_out, Write, Write_ASCII;
  wire [6:0] ASCII;
  wire [7:0] counter_1_q;
  wire [23:0] Dir_INPUT, Dir_MEMORY;
  wire [31:0] INPUT, MEMORY_IN, MEMORY_OUT;

  Button button_1 (.out(button_1_out));
  Clock clock_1 (.out(CLK));
  D_Flip_Flop d_ff_1 (.clk(CLK), .D(1'b1), .Q(d_ff_1_q), .reset(button_1_out));  // open: Qn, preset, en
  D_Flip_Flop d_ff_2 (.clk(CLK), .D(d_ff_1_q), .Qn(CLR), .reset(button_1_out));  // open: Q, preset, en
  BIG_ASM big_asm_1 (
    .DATA_INPUT(INPUT), .MEMORY_IN(MEMORY_OUT), .CLK(CLK), .CLR(CLR), .DIR_INPUT(Dir_INPUT),
    .MEMORY_OUT(MEMORY_IN), .DIR_MEMORY(Dir_MEMORY), .Write_OUTPUT(Write), .ASCII(ASCII),
    .Write_ASCII(Write_ASCII), .END(out_1));
  MEMORY memory_1 (.DIR(Dir_MEMORY), .DATA_IN(MEMORY_IN), .WRITE(Write), .CLK(CLK), .CLR(CLR), .DATA_OUT(MEMORY_OUT));
  INPUT input_1 (.DIR(Dir_INPUT), .CLK(CLK), .DATA_OUT(INPUT));
  Counter counter_1 (.load(1'b0), .count(not_1_out), .Q(counter_1_q), .clk(CLK), .clr(CLR));  // open: D, carry
  not not_1 (not_1_out, out_1);
  // Probe on counter_1_q
  TTY #(.rows(32), .cols(60)) tty_1 (.data(ASCII), .clk(CLK), .we(Write_ASCII), .clr(CLR));

  // Other names for the same wires on the sheet: END = out_1

  // Notes on the sheet:
  //   COUNTER
  //   BOARD
endmodule

module INPUT (
  input  [23:0] DIR,
  input  CLK,
  output [31:0] DATA_OUT
);

  RAM #(.addrWidth(24), .dataWidth(32)) ram_1 (.addr(DIR), .data(DATA_OUT), .clk(CLK), .ld(1'b1));  // open: sel, clr
endmodule

module MEMORY (
  input  [23:0] DIR,
  input  [31:0] DATA_IN,
  input  WRITE,
  input  CLK,
  input  CLR,
  output [31:0] DATA_OUT
);

  wire not_1_out;

  not not_1 (not_1_out, WRITE);
  RAM #(.addrWidth(24), .dataWidth(32), .bus("separate")) ram_1 (
    .addr(DIR), .din(DATA_IN), .data(DATA_OUT), .clk(CLK), .ld(not_1_out), .clr(CLR));  // open: str, sel
endmodule

module BIG_ASM (
  input  [31:0] DATA_INPUT,
  input  [31:0] MEMORY_IN,
  input  CLK,
  input  CLR,
  output [23:0] DIR_INPUT,
  output [31:0] MEMORY_OUT,
  output [23:0] DIR_MEMORY,
  output Write_OUTPUT,
  output [6:0] ASCII,
  output Write_ASCII,
  output END
);

  wire data_path_1_b____0, data_path_1_b____n, data_path_1_val____input, data_path_1_val___input,
       data_path_1_val___input_2, L_A, L_B, L_N, L_Val;
  wire [1:0] S_A, S_B;
  wire [31:0] data_path_1_a;

  DATA_PATH data_path_1 (
    .INPUT(DATA_INPUT), .CLR(CLR), .L_N(L_N), .L_Val(L_Val), .L_A(L_A), .S_A(S_A), .L_B(L_B), .S_B(S_B),
    .DIR_INPUT(DIR_INPUT), .B____N(data_path_1_b____n), .Val___INPUT(data_path_1_val___input),
    .Val____INPUT(data_path_1_val____input), .Val___INPUT_2(data_path_1_val___input_2), .CLK(CLK),
    .B____0(data_path_1_b____0), .A(data_path_1_a));
  CONTROL_UNIT control_unit_1 (
    .CLK(CLK), .Val___INPUT(data_path_1_val___input), .A(data_path_1_a), .CLR(CLR),
    .Val____INPUT(data_path_1_val____input), .B____N(data_path_1_b____n),
    .Val___INPUT_2(data_path_1_val___input_2), .B____0(data_path_1_b____0), .L_N(L_N), .S_A(S_A), .L_A(L_A),
    .S_B(S_B), .L_B(L_B), .L_Val(L_Val), .WASCII(Write_ASCII), .END(END), .ASCII(ASCII));

  // Other names for the same wires on the sheet: INPUT[31:0] = DATA_INPUT; WASCII = Write_ASCII
endmodule

module PRINT_UDEC (
  input  [31:0] num,
  input  start,
  input  CLK,
  input  RST,
  output [6:0] ASCII,
  output Write_ASCII,
  output \end 
);

  wire _0_c, _0_n, demultiplexer_1_out0, demultiplexer_2_out0, demultiplexer_2_out1, demultiplexer_3_out0,
       demultiplexer_3_out1, IDLE_2_q, IDLE_3_q, IDLE_4_q, IDLE_q, Lc, Lc_0, Ln, Ln_0, or_1_out;
  wire [23:0] bit_extender_1_out;
  wire [31:0] c, c___1, c___1_t, divider_1_rem, memory_1_data_out, multiplexer_1_out, multiplexer_2_out,
       multiplexer_3_out, n, n___10, n___10___48;

  Multiplexer #(.width(32), .enable("false")) multiplexer_1 (
    .in0(num), .in1(n___10), .out(multiplexer_1_out), .sel(Lc_0));
  Divider #(.width(32)) divider_1 (.a(n), .b(32'ha), .out(n___10), .rem(divider_1_rem));  // open: upper
  Adder #(.width(32)) adder_1 (.a(divider_1_rem), .b(32'h30), .out(n___10___48));  // open: cin, cout
  or or_1 (or_1_out, demultiplexer_1_out0, \end );
  Register #(.width(32)) u_n (.D(multiplexer_1_out), .en(Ln), .Q(n), .clk(CLK), .clr(RST));
  D_Flip_Flop IDLE (.clk(CLK), .D(or_1_out), .Q(IDLE_q), .preset(RST));  // open: Qn, en, reset
  Demultiplexer #(.enable("false")) demultiplexer_1 (
    .out0(demultiplexer_1_out0), .out1(Ln_0), .in(IDLE_q), .sel(start));
  or or_2 (Write_ASCII, demultiplexer_3_out0, demultiplexer_2_out1);
  Multiplexer #(.width(32), .enable("false")) multiplexer_2 (
    .in0(c___1), .in1(c___1_t), .out(multiplexer_2_out), .sel(Write_ASCII));
  Adder #(.width(32)) adder_2 (.a(c), .b(32'h1), .out(c___1));  // open: cin, cout
  Subtractor #(.width(32)) subtractor_1 (.a(c), .b(32'h1), .out(c___1_t));  // open: bin, bout
  D_Flip_Flop IDLE_2 (.clk(CLK), .D(Ln_0), .Q(IDLE_2_q), .reset(RST));  // open: Qn, preset, en
  Register #(.width(32)) u_c (.D(multiplexer_2_out), .en(Lc), .Q(c), .clk(CLK), .clr(RST));
  or or_3 (Lc_0, IDLE_2_q, demultiplexer_3_out1);
  Multiplexer #(.width(32), .enable("false")) multiplexer_3 (
    .in0(c), .in1(c___1_t), .out(multiplexer_3_out), .sel(Write_ASCII));
  Comparator #(.width(32), .mode("unsigned")) comparator_1 (.a({32{1'b0}}), .b(n), .lt(_0_n));  // open: gt, eq
  Comparator #(.width(32), .mode("unsigned")) comparator_2 (.a({32{1'b0}}), .b(c), .lt(_0_c));  // open: gt, eq
  D_Flip_Flop IDLE_3 (.clk(CLK), .D(Write_ASCII), .Q(IDLE_3_q), .reset(RST));  // open: Qn, preset, en
  Demultiplexer #(.enable("false")) demultiplexer_2 (
    .out0(demultiplexer_2_out0), .out1(demultiplexer_2_out1), .in(IDLE_3_q), .sel(_0_c));
  Bit_Extender #(.in_width(32), .out_width(24)) bit_extender_1 (.in(multiplexer_3_out), .out(bit_extender_1_out));
  D_Flip_Flop IDLE_4 (.clk(CLK), .D(Lc_0), .Q(IDLE_4_q), .reset(RST));  // open: Qn, preset, en
  or or_4 (Lc, Lc_0, Write_ASCII);
  or or_5 (Ln, Ln_0, Lc_0);
  Demultiplexer #(.enable("false")) demultiplexer_3 (
    .out0(demultiplexer_3_out0), .out1(demultiplexer_3_out1), .in(IDLE_4_q), .sel(_0_n));
  D_Flip_Flop IDLE_5 (.clk(CLK), .D(demultiplexer_2_out0), .Q(\end ), .reset(RST));  // open: Qn, preset, en
  MEMORY memory_1 (
    .DIR(bit_extender_1_out), .DATA_IN(n___10___48), .WRITE(Lc_0), .CLK(CLK), .CLR(RST),
    .DATA_OUT(memory_1_data_out));
  Bit_Extender #(.in_width(32), .out_width(7)) bit_extender_2 (.in(memory_1_data_out), .out(ASCII));

  // Other names for the same wires on the sheet: Lc_1 = Write_ASCII; Sc = Write_ASCII; Ln_1 = Lc_0; Sn = Lc_0;
  //   Write = Lc_0
endmodule

module PRINT_DEC (
  input  [31:0] num,
  input  start,
  input  CLK,
  input  RST,
  output [6:0] ASCII,
  output Write_ASCII,
  output END
);

  wire demultiplexer_1_out0, demultiplexer_1_out1, demultiplexer_2_out0, demultiplexer_3_out0, end_t,
       IDLE_3_q, IDLE_q, or_1_out, or_2_out, or_3_out, S_ASCII, startUDEC, Write_ASCII_1;
  wire [6:0] ASCII_t;
  wire [31:0] multiplexer_1_out, negator_1_out;

  or or_1 (or_1_out, demultiplexer_1_out0, END);
  Negator #(.width(32)) negator_1 (.in(num), .out(negator_1_out));
  D_Flip_Flop IDLE (.clk(CLK), .D(or_1_out), .Q(IDLE_q), .preset(RST));  // open: Qn, en, reset
  Demultiplexer #(.enable("false")) demultiplexer_1 (
    .out0(demultiplexer_1_out0), .out1(demultiplexer_1_out1), .in(IDLE_q), .sel(start));
  Multiplexer #(.width(32), .enable("false")) multiplexer_1 (
    .in0(num), .in1(negator_1_out), .out(multiplexer_1_out), .sel(num[31]));
  Demultiplexer #(.enable("false")) demultiplexer_2 (
    .out0(demultiplexer_2_out0), .out1(S_ASCII), .in(demultiplexer_1_out1), .sel(num[31]));
  or or_2 (or_2_out, demultiplexer_2_out0, S_ASCII);
  D_Flip_Flop IDLE_2 (.clk(CLK), .D(or_2_out), .Q(startUDEC), .reset(RST));  // open: Qn, preset, en
  PRINT_UDEC print_udec_1 (
    .num(multiplexer_1_out), .start(startUDEC), .CLK(CLK), .RST(RST), .ASCII(ASCII_t),
    .Write_ASCII(Write_ASCII_1), .\end (end_t));
  D_Flip_Flop IDLE_3 (.clk(CLK), .D(or_3_out), .Q(IDLE_3_q), .reset(RST));  // open: Qn, preset, en
  or or_3 (or_3_out, startUDEC, demultiplexer_3_out0);
  Demultiplexer #(.enable("false")) demultiplexer_3 (
    .out0(demultiplexer_3_out0), .out1(END), .in(IDLE_3_q), .sel(end_t));
  Multiplexer #(.width(7), .enable("false")) multiplexer_2 (
    .in0(ASCII_t), .in1(7'b0101101), .out(ASCII), .sel(S_ASCII));
  or or_4 (Write_ASCII, S_ASCII, Write_ASCII_1);

  // Other names for the same wires on the sheet: sign = num[31]; Write_ASCII_0 = S_ASCII
endmodule

module TEST_PRINT (
  input  [31:0] in_1,
  output out_2
);

  wire button_1_out, button_2_out, CLK, CLR, d_ff_1_q, Write_ASCII;
  wire [6:0] ASCII;

  Button button_1 (.out(button_1_out));
  Clock clock_1 (.out(CLK));
  D_Flip_Flop d_ff_1 (.clk(CLK), .D(1'b1), .Q(d_ff_1_q), .reset(button_1_out));  // open: Qn, preset, en
  D_Flip_Flop d_ff_2 (.clk(CLK), .D(d_ff_1_q), .Qn(CLR), .reset(button_1_out));  // open: Q, preset, en
  Button button_2 (.out(button_2_out));
  PRINT_UDEC print_udec_1 ();  // open: num, start, CLK, RST, ASCII, Write_ASCII, end
  PRINT_DEC print_dec_1 (
    .num(in_1), .start(button_2_out), .CLK(CLK), .RST(CLR), .ASCII(ASCII), .Write_ASCII(Write_ASCII),
    .END(out_2));
  TTY #(.rows(32), .cols(60)) tty_1 (.data(ASCII), .clk(CLK), .we(Write_ASCII), .clr(CLR));
endmodule

module DATA_PATH (
  input  [31:0] INPUT,
  input  CLK,
  input  CLR,
  input  L_N,
  input  L_Val,
  input  L_A,
  input  [1:0] S_A,
  input  L_B,
  input  [1:0] S_B,
  output [23:0] DIR_INPUT,
  output [31:0] A,
  output B____0,
  output B____N,
  output Val___INPUT,
  output Val____INPUT,
  output Val___INPUT_2
);

  wire comparator_2_eq, comparator_2_lt, comparator_3_eq;
  wire [31:0] _2___A, _2___A___1, A___1, A___2, B, multiplexer_1_out, multiplexer_2_out, N, N___1, Val;

  Register #(.width(32)) u_N (.D(INPUT), .en(L_N), .Q(N), .clk(CLK), .clr(CLR));
  Register #(.width(32)) u_Val (.D(INPUT), .en(L_Val), .Q(Val), .clk(CLK), .clr(CLR));
  Multiplexer #(.select(2), .width(32), .enable("false")) multiplexer_1 (
    .in0(32'h1), .in1(B), .in2(A___1), .out(multiplexer_1_out), .sel(S_A));  // open: in3
  Adder #(.width(32)) adder_1 (.a(N), .b(32'h1), .out(N___1));  // open: cin, cout
  Multiplier #(.width(32)) multiplier_1 (.a(32'h2), .b(A), .out(_2___A));  // open: cin, cout
  Adder #(.width(32)) adder_2 (.a(_2___A), .b(32'h1), .out(_2___A___1));  // open: cin, cout
  Divider #(.width(32)) divider_1 (.a(A), .b(32'h2), .out(A___2));  // open: upper, rem
  Subtractor #(.width(32)) subtractor_1 (.a(A), .b(32'h1), .out(A___1));  // open: bin, bout
  Register #(.width(32)) u_A (.D(multiplexer_1_out), .en(L_A), .Q(A), .clk(CLK), .clr(CLR));
  Register #(.width(32)) u_B (.D(multiplexer_2_out), .en(L_B), .Q(B), .clk(CLK), .clr(CLR));
  Multiplexer #(.select(2), .width(32), .enable("false")) multiplexer_2 (
    .in0(32'h1), .in1(_2___A), .in2(_2___A___1), .in3(A___2), .out(multiplexer_2_out), .sel(S_B));
  Multiplexer #(.width(24), .enable("false")) multiplexer_3 (
    .in0(A[23:0]), .in1(N___1[23:0]), .out(DIR_INPUT), .sel(L_Val));
  Comparator #(.width(32), .mode("unsigned")) comparator_1 (.a(B), .b({32{1'b0}}), .eq(B____0));  // open: gt, lt
  Comparator #(.width(32), .mode("unsigned")) comparator_2 (
    .a(B), .b(N), .eq(comparator_2_eq), .lt(comparator_2_lt));  // open: gt
  or or_1 (B____N, comparator_2_eq, comparator_2_lt);
  not not_1 (Val____INPUT, comparator_3_eq);
  Comparator #(.width(32), .mode("unsigned")) comparator_3 (
    .a(Val), .b(INPUT), .gt(Val___INPUT), .eq(comparator_3_eq), .lt(Val___INPUT_2));
endmodule

module CONTROL_UNIT (
  input  CLK,
  input  Val___INPUT,
  input  [31:0] A,
  input  CLR,
  input  Val____INPUT,
  input  B____0,
  input  Val___INPUT_2,
  input  B____N,
  output L_N,
  output L_Val,
  output [1:0] S_A,
  output [6:0] ASCII,
  output L_A,
  output WASCII,
  output END,
  output [1:0] S_B,
  output L_B
);

  wire Break, demultiplexer_1_out0, demultiplexer_2_out0, demultiplexer_4_out0, demultiplexer_5_out0,
       demultiplexer_5_out1, demultiplexer_6_out0, demultiplexer_7_out0, demultiplexer_7_out1,
       demultiplexer_8_out1, END_q, IDLE_q, L_A1, L_A2, L_B1, L_B2, L_B3, not_1_out, or_1_out, or_2_out,
       or_3_out, or_6_out, or_11_out, print_udec_1_end, WAIT_2_q, WAIT_4_q, WHILE_2_q, WHILE_q;

  or or_1 (or_1_out, demultiplexer_1_out0, demultiplexer_8_out1);
  D_Flip_Flop IDLE (.clk(CLK), .D(or_1_out), .Q(IDLE_q), .preset(CLR));  // open: Qn, en, reset
  Demultiplexer #(.enable("false")) demultiplexer_1 (
    .out0(demultiplexer_1_out0), .out1(L_N), .in(IDLE_q), .sel(not_1_out));
  not not_1 (not_1_out, CLR);
  D_Flip_Flop WAIT (.clk(CLK), .D(L_N), .Q(L_Val));  // open: Qn, preset, en, reset
  or or_2 (or_2_out, L_Val, L_B1, L_B2);
  D_Flip_Flop WHILE (.clk(CLK), .D(or_2_out), .Q(WHILE_q));  // open: Qn, preset, en, reset
  Demultiplexer #(.enable("false")) demultiplexer_2 (
    .out0(demultiplexer_2_out0), .out1(L_A1), .in(WHILE_q), .sel(B____N));
  Demultiplexer #(.enable("false")) demultiplexer_3 (
    .out0(Break), .out1(L_B2), .in(demultiplexer_4_out0), .sel(Val___INPUT));
  Demultiplexer #(.enable("false")) demultiplexer_4 (
    .out0(demultiplexer_4_out0), .out1(L_B1), .in(WAIT_2_q), .sel(Val___INPUT_2));
  D_Flip_Flop WAIT_2 (.clk(CLK), .D(L_A1), .Q(WAIT_2_q));  // open: Qn, preset, en, reset
  Demultiplexer #(.enable("false")) demultiplexer_5 (
    .out0(demultiplexer_5_out0), .out1(demultiplexer_5_out1), .in(or_3_out), .sel(Val____INPUT));
  or or_3 (or_3_out, demultiplexer_2_out0, Break);
  or or_4 (L_A, L_Val, L_A1, L_A2, S_A[1]);
  or or_5 (L_B, L_Val, L_B1, L_B2, L_B3);
  or or_6 (or_6_out, demultiplexer_5_out1, L_A2);
  Demultiplexer #(.enable("false")) demultiplexer_6 (
    .out0(demultiplexer_6_out0), .out1(L_B3), .in(WHILE_2_q), .sel(Val___INPUT));
  D_Flip_Flop WHILE_2 (.clk(CLK), .D(or_6_out), .Q(WHILE_2_q));  // open: Qn, preset, en, reset
  D_Flip_Flop WAIT_3 (.clk(CLK), .D(demultiplexer_7_out0), .Q(L_A2));  // open: Qn, preset, en, reset
  or or_7 (S_A[0], L_A1, L_A2);
  or or_8 (S_B[0], L_B1, L_B3);
  or or_9 (S_B[1], L_B2, L_B3);
  Demultiplexer #(.enable("false")) demultiplexer_7 (
    .out0(demultiplexer_7_out0), .out1(demultiplexer_7_out1), .in(L_B3), .sel(B____0));
  or or_10 (S_A[1], demultiplexer_5_out0, demultiplexer_6_out0, demultiplexer_7_out1);
  D_Flip_Flop WAIT_4 (.clk(CLK), .D(S_A[1]), .Q(WAIT_4_q));  // open: Qn, preset, en, reset
  PRINT_UDEC print_udec_1 (
    .num(A), .start(WAIT_4_q), .CLK(CLK), .RST(CLR), .ASCII(ASCII), .Write_ASCII(WASCII),
    .\end (print_udec_1_end));
  or or_11 (or_11_out, END, print_udec_1_end);
  D_Flip_Flop u_END (.clk(CLK), .D(or_11_out), .Q(END_q));  // open: Qn, preset, en, reset
  Demultiplexer #(.enable("false")) demultiplexer_8 (.out0(END), .out1(demultiplexer_8_out1), .in(END_q), .sel(CLR));

  // Other names for the same wires on the sheet: L_A0 = L_Val; L_B0 = L_Val; L_A3 = S_A[1];
  //   Val___INPUT_t = Val___INPUT_2
endmodule
