// Logisim project Fraction_Product.circ as structural Verilog
module BOARD_BIG_ASM (
  output out_1
);

  wire button_1_out, CLK, CLR, d_ff_1_q, not_1_out, Write, Write_ASCII;
  wire [6:0] ASCII;
  wire [7:0] counter_1_q;
  wire [23:0] Dir_INPUT, Dir_MEMORY;
  wire [31:0] INPUT, MEMORY_IN, MEMORY_OUT;

  Button button_1 (.out(button_1_out));
  Clock clock_1 (.out(CLK));
  D_Flip_Flop d_ff_1 (.clk(CLK), .D(1'b1), .Q(d_ff_1_q), .reset(button_1_out));  // open: Qn, preset, en
  D_Flip_Flop d_ff_2 (.clk(CLK), .D(d_ff_1_q), .Qn(CLR), .reset(button_1_out));  // open: Q, preset, en
  BIG_ASM big_asm_1 (
    .DATA_INPUT(INPUT), .MEMORY_IN(MEMORY_OUT), .CLK(CLK), .CLR(CLR), .DIR_INPUT(Dir_INPUT),
    .MEMORY_OUT(MEMORY_IN), .DIR_MEMORY(Dir_MEMORY), .Write_OUTPUT(Write), .ASCII(ASCII),
    .Write_ASCII(Write_ASCII), .END(out_1));
  MEMORY memory_1 (.DIR(Dir_MEMORY), .DATA_IN(MEMORY_IN), .WRITE(Write), .CLK(CLK), .CLR(CLR), .DATA_OUT(MEMORY_OUT));
  INPUT input_1 (.DIR(Dir_INPUT), .CLK(CLK), .DATA_OUT(INPUT));
  Counter counter_1 (.load(1'b0), .count(not_1_out), .Q(counter_1_q), .clk(CLK), .clr(CLR));  // open: D, carry
  not not_1 (not_1_out, out_1);
  // Probe on counter_1_q
  TTY #(.rows(32), .cols(60)) tty_1 (.data(ASCII), .clk(CLK), .we(Write_ASCII), .clr(CLR));

  // Other names for the same wires on the sheet: END = out_1

  // Notes on the sheet:
  //   COUNTER
  //   BOARD
endmodule

module INPUT (
  input  [23:0] DIR,
  input  CLK,
  output [31:0] DATA_OUT
);

  RAM #(.addrWidth(24), .dataWidth(32)) ram_1 (.addr(DIR), .data(DATA_OUT), .clk(CLK), .ld(1'b1));  // open: sel, clr
endmodule

module MEMORY (
  input  [23:0] DIR,
  input  [31:0] DATA_IN,
  input  WRITE,
  input  CLK,
  input  CLR,
  output [31:0] DATA_OUT
);

  RAM #(.addrWidth(24), .dataWidth(32), .bus("separate")) ram_1 (
    .addr(DIR), .din(DATA_IN), .data(DATA_OUT), .str(WRITE), .clk(CLK), .clr(CLR));  // open: sel, ld
endmodule

module BIG_ASM (
  input  [31:0] DATA_INPUT,
  input  [31:0] MEMORY_IN,
  input  CLK,
  input  CLR,
  output [23:0] DIR_INPUT,
  output [31:0] MEMORY_OUT,
  output [23:0] DIR_MEMORY,
  output Write_OUTPUT,
  output [6:0] ASCII,
  output Write_ASCII,
  output END
);

  wire Load_a, Load_b, Load_c, Load_D, Load_d_t, Load_N, Sel_D, Sel_N;
  wire [31:0] Den, mcd, Num;

  CONTROL_UNIT control_unit_1 (
    .Sel_N(Sel_N), .Sel_D(Sel_D), .Load_N(Load_N), .Load_D_2(Load_D), .Load_a(Load_a), .Load_b(Load_b),
    .Load_c(Load_c), .Load_d(Load_d_t), .Reset(CLR), .Clk(CLK), .Num(Num), .Den(Den), .mcd(mcd), .End(END),
    .ASCII(ASCII), .Write_ASCII(Write_ASCII));
  DATAPATH datapath_1 (
    .\input (DATA_INPUT), .Sel_D(Sel_D), .Load_a(Load_a), .Sel_N(Sel_N), .Load_b(Load_b), .Load_D(Load_D),
    .Load_c(Load_c), .Load_N(Load_N), .Load_d_2(Load_d_t), .Num(Num), .Den(Den), .mcd(mcd), .Clk(CLK),
    .DIR_MEMORY(DIR_INPUT), .Clr(CLR));

  // Other names for the same wires on the sheet: ASCII_t = Write_ASCII; INPUT[31:0] = DATA_INPUT; PRINT = END;
  //   Reset = CLR; WASCII[6:0] = ASCII
endmodule

module PRINT_UDEC (
  input  [31:0] num,
  input  start,
  input  CLK,
  input  RST,
  output [6:0] ASCII,
  output Write_ASCII,
  output \end 
);

  wire _0_c, _0_n, demultiplexer_1_out0, demultiplexer_2_out0, demultiplexer_2_out1, demultiplexer_3_out0,
       demultiplexer_3_out1, IDLE_2_q, IDLE_3_q, IDLE_4_q, IDLE_q, Lc, Lc_0, Ln, Ln_0, or_1_out;
  wire [23:0] bit_extender_1_out;
  wire [31:0] c, c___1, c___1_t, divider_1_rem, memory_1_data_out, multiplexer_1_out, multiplexer_2_out,
       multiplexer_3_out, n, n___10, n___10___48;

  Multiplexer #(.width(32), .enable("false")) multiplexer_1 (
    .in0(num), .in1(n___10), .out(multiplexer_1_out), .sel(Lc_0));
  Divider #(.width(32)) divider_1 (.a(n), .b(32'ha), .out(n___10), .rem(divider_1_rem));  // open: upper
  Adder #(.width(32)) adder_1 (.a(divider_1_rem), .b(32'h30), .out(n___10___48));  // open: cin, cout
  or or_1 (or_1_out, demultiplexer_1_out0, \end );
  Register #(.width(32)) u_n (.D(multiplexer_1_out), .en(Ln), .Q(n), .clk(CLK), .clr(RST));
  D_Flip_Flop IDLE (.clk(CLK), .D(or_1_out), .Q(IDLE_q), .preset(RST));  // open: Qn, en, reset
  Demultiplexer #(.enable("false")) demultiplexer_1 (
    .out0(demultiplexer_1_out0), .out1(Ln_0), .in(IDLE_q), .sel(start));
  or or_2 (Write_ASCII, demultiplexer_3_out0, demultiplexer_2_out1);
  Multiplexer #(.width(32), .enable("false")) multiplexer_2 (
    .in0(c___1), .in1(c___1_t), .out(multiplexer_2_out), .sel(Write_ASCII));
  Adder #(.width(32)) adder_2 (.a(c), .b(32'h1), .out(c___1));  // open: cin, cout
  Subtractor #(.width(32)) subtractor_1 (.a(c), .b(32'h1), .out(c___1_t));  // open: bin, bout
  D_Flip_Flop IDLE_2 (.clk(CLK), .D(Ln_0), .Q(IDLE_2_q), .reset(RST));  // open: Qn, preset, en
  Register #(.width(32)) u_c (.D(multiplexer_2_out), .en(Lc), .Q(c), .clk(CLK), .clr(RST));
  or or_3 (Lc_0, IDLE_2_q, demultiplexer_3_out1);
  Multiplexer #(.width(32), .enable("false")) multiplexer_3 (
    .in0(c), .in1(c___1_t), .out(multiplexer_3_out), .sel(Write_ASCII));
  Comparator #(.width(32), .mode("unsigned")) comparator_1 (.a({32{1'b0}}), .b(n), .lt(_0_n));  // open: gt, eq
  Comparator #(.width(32), .mode("unsigned")) comparator_2 (.a({32{1'b0}}), .b(c), .lt(_0_c));  // open: gt, eq
  D_Flip_Flop IDLE_3 (.clk(CLK), .D(Write_ASCII), .Q(IDLE_3_q), .reset(RST));  // open: Qn, preset, en
  Demultiplexer #(.enable("false")) demultiplexer_2 (
    .out0(demultiplexer_2_out0), .out1(demultiplexer_2_out1), .in(IDLE_3_q), .sel(_0_c));
  Bit_Extender #(.in_width(32), .out_width(24)) bit_extender_1 (.in(multiplexer_3_out), .out(bit_extender_1_out));
  D_Flip_Flop IDLE_4 (.clk(CLK), .D(Lc_0), .Q(IDLE_4_q), .reset(RST));  // open: Qn, preset, en
  or or_4 (Lc, Lc_0, Write_ASCII);
  or or_5 (Ln, Ln_0, Lc_0);
  Demultiplexer #(.enable("false")) demultiplexer_3 (
    .out0(demultiplexer_3_out0), .out1(demultiplexer_3_out1), .in(IDLE_4_q), .sel(_0_n));
  D_Flip_Flop IDLE_5 (.clk(CLK), .D(demultiplexer_2_out0), .Q(\end ), .reset(RST));  // open: Qn, preset, en
  MEMORY memory_1 (
    .DIR(bit_extender_1_out), .DATA_IN(n___10___48), .WRITE(Lc_0), .CLK(CLK), .CLR(RST),
    .DATA_OUT(memory_1_data_out));
  Bit_Extender #(.in_width(32), .out_width(7)) bit_extender_2 (.in(memory_1_data_out), .out(ASCII));

  // Other names for the same wires on the sheet: Lc_1 = Write_ASCII; Sc = Write_ASCII; Ln_1 = Lc_0; Sn = Lc_0;
  //   Write = Lc_0
endmodule

module PRINT_DEC (
  input  [31:0] num,
  input  start,
  input  CLK,
  input  RST,
  output [6:0] ASCII,
  output Write_ASCII,
  output END
);

  wire demultiplexer_1_out0, demultiplexer_1_out1, demultiplexer_2_out0, demultiplexer_3_out0, end_t,
       IDLE_3_q, IDLE_q, or_1_out, or_2_out, or_3_out, S_ASCII, startUDEC, Write_ASCII_1;
  wire [6:0] ASCII_t;
  wire [31:0] multiplexer_1_out, negator_1_out;

  or or_1 (or_1_out, demultiplexer_1_out0, END);
  Negator #(.width(32)) negator_1 (.in(num), .out(negator_1_out));
  D_Flip_Flop IDLE (.clk(CLK), .D(or_1_out), .Q(IDLE_q), .preset(RST));  // open: Qn, en, reset
  Demultiplexer #(.enable("false")) demultiplexer_1 (
    .out0(demultiplexer_1_out0), .out1(demultiplexer_1_out1), .in(IDLE_q), .sel(start));
  Multiplexer #(.width(32), .enable("false")) multiplexer_1 (
    .in0(num), .in1(negator_1_out), .out(multiplexer_1_out), .sel(num[31]));
  Demultiplexer #(.enable("false")) demultiplexer_2 (
    .out0(demultiplexer_2_out0), .out1(S_ASCII), .in(demultiplexer_1_out1), .sel(num[31]));
  or or_2 (or_2_out, demultiplexer_2_out0, S_ASCII);
  D_Flip_Flop IDLE_2 (.clk(CLK), .D(or_2_out), .Q(startUDEC), .reset(RST));  // open: Qn, preset, en
  PRINT_UDEC print_udec_1 (
    .num(multiplexer_1_out), .start(startUDEC), .CLK(CLK), .RST(RST), .ASCII(ASCII_t),
    .Write_ASCII(Write_ASCII_1), .\end (end_t));
  D_Flip_Flop IDLE_3 (.clk(CLK), .D(or_3_out), .Q(IDLE_3_q), .reset(RST));  // open: Qn, preset, en
  or or_3 (or_3_out, startUDEC, demultiplexer_3_out0);
  Demultiplexer #(.enable("false")) demultiplexer_3 (
    .out0(demultiplexer_3_out0), .out1(END), .in(IDLE_3_q), .sel(end_t));
  Multiplexer #(.width(7), .enable("false")) multiplexer_2 (
    .in0(ASCII_t), .in1(7'b0101101), .out(ASCII), .sel(S_ASCII));
  or or_4 (Write_ASCII, S_ASCII, Write_ASCII_1);

  // Other names for the same wires on the sheet: sign = num[31]; Write_ASCII_0 = S_ASCII
endmodule

module TEST_PRINT (
  input  [31:0] in_1,
  output out_2
);

  wire button_1_out, button_2_out, CLK, CLR, d_ff_1_q, Write_ASCII;
  wire [6:0] ASCII;

  Button button_1 (.out(button_1_out));
  Clock clock_1 (.out(CLK));
  D_Flip_Flop d_ff_1 (.clk(CLK), .D(1'b1), .Q(d_ff_1_q), .reset(button_1_out));  // open: Qn, preset, en
  D_Flip_Flop d_ff_2 (.clk(CLK), .D(d_ff_1_q), .Qn(CLR), .reset(button_1_out));  // open: Q, preset, en
  Button button_2 (.out(button_2_out));
  PRINT_UDEC print_udec_1 ();  // open: num, start, CLK, RST, ASCII, Write_ASCII, end
  PRINT_DEC print_dec_1 (
    .num(in_1), .start(button_2_out), .CLK(CLK), .RST(CLR), .ASCII(ASCII), .Write_ASCII(Write_ASCII),
    .END(out_2));
  TTY #(.rows(32), .cols(60)) tty_1 (.data(ASCII), .clk(CLK), .we(Write_ASCII), .clr(CLR));
endmodule

module DataPath (
  input  SA,
  input  in_2,
  input  [31:0] a,
  input  [1:0] SB,
  input  in_5,
  input  [31:0] b,
  output [31:0] A_2,
  output [31:0] B_2,
  output out_9,
  output out_10
);

  wire clock_1_out, clock_2_out, comparator_1_eq;
  wire [31:0] B_A, multiplexer_1_out, multiplexer_2_out;

  Multiplexer #(.width(32), .enable("false")) multiplexer_1 (.in0(a), .in1(B_2), .out(multiplexer_1_out), .sel(SA));
  Subtractor #(.width(32)) subtractor_1 (.a(B_2), .b(A_2), .out(B_A));  // open: bin, bout
  // Probe on B_A
  Register #(.width(32)) register_1 (.D(multiplexer_1_out), .en(in_2), .Q(A_2), .clk(clock_1_out));  // open: clr
  Clock clock_1 (.out(clock_1_out));
  Comparator #(.width(32), .mode("unsigned")) comparator_1 (
    .a(A_2), .b(B_2), .gt(out_10), .eq(comparator_1_eq));  // open: lt
  Multiplexer #(.select(2), .width(32), .enable("false")) multiplexer_2 (
    .in0(b), .in1(A_2), .in2(B_A), .out(multiplexer_2_out), .sel(SB));  // open: in3
  not not_1 (out_9, comparator_1_eq);
  // Probe on B_2
  Register #(.width(32)) register_2 (.D(multiplexer_2_out), .en(in_5), .Q(B_2), .clk(clock_2_out));  // open: clr
  Clock clock_2 (.out(clock_2_out));

  // Other names for the same wires on the sheet: A__B = out_9; A_B = out_10; A_t[31:0] = A_2; B_t[31:0] = B_2;
  //   LA = in_2; LB = in_5
endmodule

module Control_Unit (
  input  A__B,
  input  A_B,
  input  Start,
  input  Clk,
  input  Reset,
  output [1:0] SB,
  output LA,
  output LB,
  output SA,
  output End
);

  wire d_ff_1_q, demultiplexer_1_out0, demultiplexer_2_out0, demultiplexer_2_out1, demultiplexer_3_out0,
       demultiplexer_4_out0, demultiplexer_4_out1, LA0, or_1_out, or_3_out, or_5_out, or_6_out, Start_q;

  or or_1 (or_1_out, demultiplexer_1_out0, demultiplexer_4_out1);
  D_Flip_Flop u_Start (.clk(Clk), .D(or_1_out), .Q(Start_q), .preset(Reset));  // open: Qn, en, reset
  Demultiplexer #(.enable("false")) demultiplexer_1 (
    .out0(demultiplexer_1_out0), .out1(LA0), .in(Start_q), .sel(Start));
  or or_2 (LA, LA0, SA);
  or or_3 (or_3_out, LA0, SB[1]);
  D_Flip_Flop d_ff_1 (.clk(Clk), .D(or_3_out), .Q(d_ff_1_q));  // open: Qn, preset, en, reset
  Demultiplexer #(.enable("false")) demultiplexer_2 (
    .out0(demultiplexer_2_out0), .out1(demultiplexer_2_out1), .in(d_ff_1_q), .sel(A__B));
  Demultiplexer #(.enable("false")) demultiplexer_3 (
    .out0(demultiplexer_3_out0), .out1(SA), .in(demultiplexer_2_out1), .sel(A_B));
  or or_4 (LB, LA0, SA, SB[1]);
  or or_5 (or_5_out, demultiplexer_4_out0, demultiplexer_2_out0);
  D_Flip_Flop d_ff_2 (.clk(Clk), .D(or_5_out), .Q(End));  // open: Qn, preset, en, reset
  Demultiplexer #(.enable("false")) demultiplexer_4 (
    .out0(demultiplexer_4_out0), .out1(demultiplexer_4_out1), .in(End), .sel(Reset));
  or or_6 (or_6_out, demultiplexer_3_out0, SA);
  D_Flip_Flop d_ff_3 (.clk(Clk), .D(or_6_out), .Q(SB[1]));  // open: Qn, preset, en, reset

  assign SB[0] = SA;

  // Other names for the same wires on the sheet: LB0 = LA0; LA1 = SA; LB1 = SA; SB0 = SA; LB2 = SB[1]
endmodule

module DATAPATH (
  input  [31:0] \input ,
  input  [31:0] mcd,
  input  Sel_D,
  input  Load_a,
  input  Sel_N,
  input  Load_b,
  input  Load_D,
  input  Load_c,
  input  Load_N,
  input  Load_d_2,
  input  Clk,
  input  Clr,
  output [23:0] DIR_MEMORY,
  output [31:0] Num,
  output [31:0] Den
);

  wire or_1_out;
  wire [31:0] A, a_X_c, B, b_X_d, C, D, den_mcd, Input_t, multiplexer_1_out, multiplexer_2_out, num_mcd;

  Register #(.width(32)) register_1 (.D(Input_t), .en(Load_a), .Q(A), .clk(Clk), .clr(Clr));
  Multiplexer #(.width(32), .enable("false")) multiplexer_1 (
    .in0(a_X_c), .in1(num_mcd), .out(multiplexer_1_out), .sel(Sel_N));
  Multiplier #(.width(32)) multiplier_1 (.a(A), .b(C), .out(a_X_c));  // open: cin, cout
  Divider #(.width(32)) divider_1 (.a(a_X_c), .b(mcd), .out(num_mcd));  // open: upper, rem
  Register #(.width(32)) register_2 (.D(multiplexer_1_out), .en(Load_N), .Q(Num), .clk(Clk), .clr(Clr));
  Multiplier #(.width(32)) multiplier_2 (.a(B), .b(D), .out(b_X_d));  // open: cin, cout
  Register #(.width(32)) register_3 (.D(Input_t), .en(Load_b), .Q(B), .clk(Clk), .clr(Clr));
  Divider #(.width(32)) divider_2 (.a(b_X_d), .b(mcd), .out(den_mcd));  // open: upper, rem
  Register #(.width(32)) register_4 (.D(Input_t), .en(Load_c), .Q(C), .clk(Clk), .clr(Clr));
  Multiplexer #(.width(32), .enable("false")) multiplexer_2 (
    .in0(b_X_d), .in1(den_mcd), .out(multiplexer_2_out), .sel(Sel_D));
  Register #(.width(32)) register_5 (.D(multiplexer_2_out), .en(Load_D), .Q(Den), .clk(Clk), .clr(Clr));
  Counter #(.width(24), .max('hffffff)) u_DIR_MEMORY (
    .count(or_1_out), .Q(DIR_MEMORY), .clk(Clk), .clr(Clr));  // open: load, D, carry
  or or_1 (or_1_out, Load_a, Load_b, Load_c);
  Register #(.width(32)) register_6 (.D(Input_t), .en(Load_d_2), .Q(D), .clk(Clk), .clr(Clr));

  // Other names for the same wires on the sheet: Load_d_t = Load_d_2

  // Notes on the sheet:
  //   Multiplicacion
  //   Division
  //   Multiplicacion
  //   Division
endmodule

module CONTROL_UNIT (
  input  Reset,
  input  Clk,
  input  [31:0] Num,
  input  [31:0] Den,
  output End,
  output Sel_N,
  output Load_a,
  output [6:0] ASCII,
  output Sel_D,
  output Load_b,
  output [31:0] mcd,
  output Load_c,
  output Load_N,
  output Load_d,
  output Load_D_2,
  output Write_ASCII
);

  wire d_ff_1_q, demultiplexer_1_out0, demultiplexer_2_out0, demultiplexer_3_out1, End_t, Load_c_t, Load_D0,
       or_1_out, or_4_out, or_5_out, print_dec_2_end, Start, Start_4_q, Start_7_q, Start_q, W_ASCII_0,
       W_ASCII_1, W_ASCII_2;
  wire [6:0] ASCII_0, ASCII_1;

  not not_1 (Start, Reset);
  D_Flip_Flop u_Start (.clk(Clk), .D(or_1_out), .Q(Start_q), .preset(Reset));  // open: Qn, en, reset
  or or_1 (or_1_out, demultiplexer_1_out0, demultiplexer_3_out1);
  Demultiplexer #(.enable("false")) demultiplexer_1 (
    .out0(demultiplexer_1_out0), .out1(Load_a), .in(Start_q), .sel(Start));
  D_Flip_Flop Start_2 (.clk(Clk), .D(Load_a), .Q(Load_b));  // open: Qn, preset, en, reset
  or or_2 (Load_N, Load_D0, Sel_D);
  or or_3 (Load_D_2, Load_D0, Sel_D);
  D_Flip_Flop Start_3 (.clk(Clk), .D(Load_b), .Q(Load_c_t));  // open: Qn, preset, en, reset
  or or_4 (or_4_out, demultiplexer_2_out0, Load_D0);
  Demultiplexer #(.enable("false")) demultiplexer_2 (
    .out0(demultiplexer_2_out0), .out1(Sel_D), .in(Start_4_q), .sel(End_t));
  D_Flip_Flop Start_4 (.clk(Clk), .D(or_4_out), .Q(Start_4_q), .reset(Reset));  // open: Qn, preset, en
  D_Flip_Flop Start_5 (.clk(Clk), .D(Load_c_t), .Q(Load_d));  // open: Qn, preset, en, reset
  D_Flip_Flop Start_6 (.clk(Clk), .D(Load_d), .Q(Load_D0));  // open: Qn, preset, en, reset
  D_Flip_Flop Start_7 (.clk(Clk), .D(Load_D0), .Q(Start_7_q));  // open: Qn, preset, en, reset
  PRINT_DEC print_dec_1 (
    .num(Num), .start(Sel_D), .CLK(Clk), .RST(Reset), .ASCII(ASCII_0), .Write_ASCII(W_ASCII_0),
    .END(W_ASCII_1));
  MCD mcd_1 (.in_1(Num), .in_2(Den), .in_3(Clk), .in_4(Start_7_q), .in_5(Reset), .MCD(mcd), .End(End_t));
  PRINT_DEC print_dec_2 (
    .num(Den), .start(W_ASCII_1), .CLK(Clk), .RST(Reset), .ASCII(ASCII_1), .Write_ASCII(W_ASCII_2),
    .END(print_dec_2_end));
  or or_5 (or_5_out, End, print_dec_2_end);
  D_Flip_Flop d_ff_1 (.clk(Clk), .D(or_5_out), .Q(d_ff_1_q));  // open: Qn, preset, en, reset
  Multiplexer #(.select(2), .width(7), .enable("false")) multiplexer_1 (
    .in0(ASCII_0), .in1(7'b0100000), .in2(ASCII_1), .out(ASCII), .sel({W_ASCII_2, W_ASCII_1}));  // open: in3
  or or_6 (Write_ASCII, W_ASCII_0, W_ASCII_1, W_ASCII_2);
  Demultiplexer #(.enable("false")) demultiplexer_3 (
    .out0(End), .out1(demultiplexer_3_out1), .in(d_ff_1_q), .sel(Reset));

  assign Sel_N = Sel_D;

  // Other names for the same wires on the sheet: Load_D_t = Load_D_2; Load_N0 = Load_D0; Load_D1 = Sel_D;
  //   Load_N1 = Sel_D
endmodule

module MCD (
  input  [31:0] in_1,
  input  [31:0] in_2,
  input  in_3,
  input  in_4,
  input  in_5,
  output [31:0] MCD,
  output End
);

  wire A__B, A_B, LA, LB, SA;
  wire [1:0] SB;
  wire [31:0] B;

  Control_Unit control_unit_1 (
    .A__B(A__B), .A_B(A_B), .Start(in_4), .Clk(in_3), .Reset(in_5), .LA(LA), .LB(LB), .SA(SA), .SB(SB),
    .End(End));
  DataPath Data_Path (
    .SA(SA), .in_2(LA), .a(in_1), .in_5(LB), .b(in_2), .out_9(A__B), .out_10(A_B), .SB(SB), .A_2(MCD), .B_2(B));

  // Other names for the same wires on the sheet: A[31:0] = MCD; Clk = in_3; den[31:0] = in_2; num[31:0] = in_1;
  //   Reset = in_5; Start = in_4
endmodule
